// Logisim project cpu.circ as structural Verilog: 9 circuits, main circuit main
module base_5_encoder (
  input  _0,
  input  _1,
  input  _2,
  input  _3,
  input  _4,
  input  _5,
  input  _6,
  input  _7,
  input  _8,
  input  _9,
  input  _10,
  input  _11,
  input  _12,
  input  _13,
  input  _14,
  input  _15,
  output a,
  output b,
  output c,
  output d,
  output out_21,
  output f,
  output g,
  output a_2,
  output b_2,
  output c_2,
  output d_2,
  output e,
  output f_2,
  output g_2
);

  wire or_1_out, or_2_out, or_3_out, or_4_out, or_5_out, or_6_out, or_7_out, or_8_out, or_9_out, or_10_out,
       or_11_out, or_12_out, or_13_out, or_14_out, or_15_out, or_16_out, or_17_out, or_18_out, or_19_out,
       or_21_out, or_22_out, or_23_out, or_24_out, or_25_out, or_27_out, or_28_out, or_31_out, or_34_out;

  or or_1 (or_1_out, _0, _10);
  or or_2 (or_2_out, _1, _11);
  or or_3 (or_3_out, _2, _12);
  or or_4 (or_4_out, _3, _13);
  or or_5 (or_5_out, _4, _14);
  or or_6 (or_6_out, or_1_out, _15);
  or or_7 (or_7_out, or_6_out, _5);
  or or_8 (or_8_out, or_2_out, _6);
  or or_9 (or_9_out, or_3_out, _7);
  or or_10 (or_10_out, or_4_out, _8);
  or or_11 (or_11_out, or_5_out, _9);
  or or_12 (or_12_out, _3, _4);
  or or_13 (or_13_out, _8, _9);
  or or_14 (or_14_out, _13, _14);
  or or_15 (or_15_out, or_4_out, or_5_out);
  or or_16 (or_16_out, _2, or_12_out);
  or or_17 (or_17_out, _7, or_13_out);
  or or_18 (or_18_out, _12, or_14_out);
  or or_19 (or_19_out, or_3_out, or_15_out);
  or or_20 (e, or_9_out, or_7_out);
  or or_21 (or_21_out, or_10_out, or_11_out);
  or or_22 (or_22_out, _1, or_16_out);
  or or_23 (or_23_out, _6, or_17_out);
  or or_24 (or_24_out, _11, or_18_out);
  or or_25 (or_25_out, or_2_out, or_19_out);
  or or_26 (f, _0, or_22_out);
  or or_27 (or_27_out, _5, or_23_out);
  or or_28 (or_28_out, _10, or_24_out);
  or or_29 (out_21, or_1_out, or_25_out);
  or or_30 (a_2, or_10_out, e);
  or or_31 (or_31_out, or_21_out, or_7_out);
  or or_32 (f_2, or_11_out, or_7_out);
  or or_33 (g_2, or_21_out, or_9_out);
  or or_34 (or_34_out, _15, or_27_out);
  or or_35 (g, _15, or_28_out);
  or or_36 (c_2, or_8_out, or_31_out);
  or or_37 (a, out_21, _15);
  or or_38 (c, or_34_out, f);
  or or_39 (b, e, c_2);

  assign b_2 = b;
  assign d = a;
  assign d_2 = a_2;

  // Notes on the sheet:
  //   Fives digit
  //   Ones digit
  //   e
endmodule

module main (
  input  in_1,
  output Overflow_error
);

  wire base_2_decoder_1_a, base_2_decoder_1_a_2, base_2_decoder_1_b, base_2_decoder_1_b_2,
       base_2_decoder_1_c, base_2_decoder_1_c_2, base_2_decoder_1_e, base_2_decoder_1_e_2,
       base_2_decoder_1_f, base_2_decoder_1_f_2, base_2_decoder_1_g, base_2_decoder_1_g_2,
       base_2_decoder_1_out_8, base_2_decoder_1_out_15, base_2_encoder_1_a0, base_2_encoder_1_a1,
       base_2_encoder_1_a2, base_2_encoder_1_a3, base_2_encoder_2_a0, base_2_encoder_2_a1,
       base_2_encoder_2_a2, base_2_encoder_2_a3, base_5_encoder_1_a, base_5_encoder_1_a_2,
       base_5_encoder_1_b, base_5_encoder_1_b_2, base_5_encoder_1_c, base_5_encoder_1_c_2,
       base_5_encoder_1_d, base_5_encoder_1_d_2, base_5_encoder_1_e, base_5_encoder_1_f,
       base_5_encoder_1_f_2, base_5_encoder_1_g, base_5_encoder_1_g_2, base_5_encoder_1_out_21,
       base_5_encoder_2_a, base_5_encoder_2_a_2, base_5_encoder_2_b, base_5_encoder_2_b_2,
       base_5_encoder_2_c, base_5_encoder_2_c_2, base_5_encoder_2_d, base_5_encoder_2_d_2,
       base_5_encoder_2_e, base_5_encoder_2_f, base_5_encoder_2_f_2, base_5_encoder_2_g,
       base_5_encoder_2_g_2, base_5_encoder_2_out_21, calculator_1_out_11, calculator_1_out_12,
       calculator_1_out_13, calculator_1_out_14, dipswitch_1_sw1, dipswitch_1_sw2, dipswitch_1_sw3,
       dipswitch_1_sw4, dipswitch_1_sw5, dipswitch_1_sw6, dipswitch_1_sw7, dipswitch_1_sw8, dipswitch_1_sw9,
       dipswitch_1_sw10, dipswitch_1_sw11, dipswitch_1_sw12, dipswitch_1_sw13, dipswitch_1_sw14,
       dipswitch_1_sw15, dipswitch_1_sw16, dipswitch_2_sw1, dipswitch_2_sw2, dipswitch_2_sw3,
       dipswitch_2_sw4, dipswitch_2_sw5, dipswitch_2_sw6, dipswitch_2_sw7, dipswitch_2_sw8, dipswitch_2_sw9,
       dipswitch_2_sw10, dipswitch_2_sw11, dipswitch_2_sw12, dipswitch_2_sw13, dipswitch_2_sw14,
       dipswitch_2_sw15, dipswitch_2_sw16;
  wire [4:0] operator_1_c0, operator_1_c1, operator_1_c2, operator_1_c3, operator_1_out_6;

  base_5_encoder base_5_encoder_1 (
    .a_2(base_5_encoder_1_a_2), .b_2(base_5_encoder_1_b_2), .c_2(base_5_encoder_1_c_2),
    .d_2(base_5_encoder_1_d_2), .e(base_5_encoder_1_e), .f_2(base_5_encoder_1_f_2),
    .g_2(base_5_encoder_1_g_2), .a(base_5_encoder_1_a), .b(base_5_encoder_1_b), .c(base_5_encoder_1_c),
    .d(base_5_encoder_1_d), .out_21(base_5_encoder_1_out_21), .f(base_5_encoder_1_f), .g(base_5_encoder_1_g),
    ._1(dipswitch_1_sw2), ._2(dipswitch_1_sw3), ._3(dipswitch_1_sw4), ._4(dipswitch_1_sw5),
    ._5(dipswitch_1_sw6), ._6(dipswitch_1_sw7), ._7(dipswitch_1_sw8), ._8(dipswitch_1_sw9),
    ._9(dipswitch_1_sw10), ._10(dipswitch_1_sw11), ._11(dipswitch_1_sw12), ._12(dipswitch_1_sw13),
    ._13(dipswitch_1_sw14), ._14(dipswitch_1_sw15), ._15(dipswitch_1_sw16), ._0(dipswitch_1_sw1));
  DipSwitch #(.number(16)) dipswitch_1 (
    .sw1(dipswitch_1_sw1), .sw2(dipswitch_1_sw2), .sw3(dipswitch_1_sw3), .sw4(dipswitch_1_sw4),
    .sw5(dipswitch_1_sw5), .sw6(dipswitch_1_sw6), .sw7(dipswitch_1_sw7), .sw8(dipswitch_1_sw8),
    .sw9(dipswitch_1_sw9), .sw10(dipswitch_1_sw10), .sw11(dipswitch_1_sw11), .sw12(dipswitch_1_sw12),
    .sw13(dipswitch_1_sw13), .sw14(dipswitch_1_sw14), .sw15(dipswitch_1_sw15), .sw16(dipswitch_1_sw16));
  _7_Segment_Display u_7_segment_display_1 (
    .g(base_5_encoder_1_g), .f(base_5_encoder_1_f), .a(base_5_encoder_1_a), .b(base_5_encoder_1_b),
    .e(base_5_encoder_1_out_21), .d(base_5_encoder_1_d), .c(base_5_encoder_1_c));  // open: dp
  _7_Segment_Display u_7_segment_display_2 (
    .g(base_5_encoder_1_g_2), .f(base_5_encoder_1_f_2), .a(base_5_encoder_1_a_2), .b(base_5_encoder_1_b_2),
    .e(base_5_encoder_1_e), .d(base_5_encoder_1_d_2), .c(base_5_encoder_1_c_2));  // open: dp
  DotMatrix #(.matrixrows(5)) dotmatrix_1 (
    .col0(operator_1_c0), .col1(operator_1_c1), .col2(operator_1_c2), .col3(operator_1_c3),
    .col4(operator_1_out_6));
  operator operator_1 (
    .c0(operator_1_c0), .c1(operator_1_c1), .c2(operator_1_c2), .c3(operator_1_c3), .out_6(operator_1_out_6),
    .in_1(in_1));
  base_2_encoder base_2_encoder_1 (
    .A0(base_2_encoder_1_a0), .A1(base_2_encoder_1_a1), .A2(base_2_encoder_1_a2), .A3(base_2_encoder_1_a3),
    ._0(dipswitch_1_sw1), ._1(dipswitch_1_sw2), ._2(dipswitch_1_sw3), ._3(dipswitch_1_sw4),
    ._4(dipswitch_1_sw5), ._5(dipswitch_1_sw6), ._6(dipswitch_1_sw7), ._7(dipswitch_1_sw8),
    ._8(dipswitch_1_sw9), ._9(dipswitch_1_sw10), ._10(dipswitch_1_sw11), ._11(dipswitch_1_sw12),
    ._12(dipswitch_1_sw13), ._13(dipswitch_1_sw14), ._14(dipswitch_1_sw15), ._15(dipswitch_1_sw16));
  base_5_encoder base_5_encoder_2 (
    .a_2(base_5_encoder_2_a_2), .b_2(base_5_encoder_2_b_2), .c_2(base_5_encoder_2_c_2),
    .d_2(base_5_encoder_2_d_2), .e(base_5_encoder_2_e), .f_2(base_5_encoder_2_f_2),
    .g_2(base_5_encoder_2_g_2), .a(base_5_encoder_2_a), .b(base_5_encoder_2_b), .c(base_5_encoder_2_c),
    .d(base_5_encoder_2_d), .out_21(base_5_encoder_2_out_21), .f(base_5_encoder_2_f), .g(base_5_encoder_2_g),
    ._1(dipswitch_2_sw2), ._2(dipswitch_2_sw3), ._3(dipswitch_2_sw4), ._4(dipswitch_2_sw5),
    ._5(dipswitch_2_sw6), ._6(dipswitch_2_sw7), ._7(dipswitch_2_sw8), ._8(dipswitch_2_sw9),
    ._9(dipswitch_2_sw10), ._10(dipswitch_2_sw11), ._11(dipswitch_2_sw12), ._12(dipswitch_2_sw13),
    ._13(dipswitch_2_sw14), ._14(dipswitch_2_sw15), ._15(dipswitch_2_sw16), ._0(dipswitch_2_sw1));
  DipSwitch #(.number(16)) dipswitch_2 (
    .sw1(dipswitch_2_sw1), .sw2(dipswitch_2_sw2), .sw3(dipswitch_2_sw3), .sw4(dipswitch_2_sw4),
    .sw5(dipswitch_2_sw5), .sw6(dipswitch_2_sw6), .sw7(dipswitch_2_sw7), .sw8(dipswitch_2_sw8),
    .sw9(dipswitch_2_sw9), .sw10(dipswitch_2_sw10), .sw11(dipswitch_2_sw11), .sw12(dipswitch_2_sw12),
    .sw13(dipswitch_2_sw13), .sw14(dipswitch_2_sw14), .sw15(dipswitch_2_sw15), .sw16(dipswitch_2_sw16));
  _7_Segment_Display u_7_segment_display_3 (
    .g(base_5_encoder_2_g), .f(base_5_encoder_2_f), .a(base_5_encoder_2_a), .b(base_5_encoder_2_b),
    .e(base_5_encoder_2_out_21), .d(base_5_encoder_2_d), .c(base_5_encoder_2_c));  // open: dp
  _7_Segment_Display u_7_segment_display_4 (
    .g(base_5_encoder_2_g_2), .f(base_5_encoder_2_f_2), .a(base_5_encoder_2_a_2), .b(base_5_encoder_2_b_2),
    .e(base_5_encoder_2_e), .d(base_5_encoder_2_d_2), .c(base_5_encoder_2_c_2));  // open: dp
  calculator calculator_1 (
    .Overflow(Overflow_error), .out_11(calculator_1_out_11), .out_12(calculator_1_out_12),
    .out_13(calculator_1_out_13), .out_14(calculator_1_out_14), .A3(base_2_encoder_1_a3),
    .B2(base_2_encoder_2_a3), .A2(base_2_encoder_1_a2), .B1(base_2_encoder_2_a2), .A1(base_2_encoder_1_a1),
    .B0(base_2_encoder_2_a1), .A0(base_2_encoder_1_a0), .in_8(base_2_encoder_2_a0), .Subtract(in_1));
  base_2_encoder base_2_encoder_2 (
    .A0(base_2_encoder_2_a0), .A1(base_2_encoder_2_a1), .A2(base_2_encoder_2_a2), .A3(base_2_encoder_2_a3),
    ._0(dipswitch_2_sw1), ._1(dipswitch_2_sw2), ._2(dipswitch_2_sw3), ._3(dipswitch_2_sw4),
    ._4(dipswitch_2_sw5), ._5(dipswitch_2_sw6), ._6(dipswitch_2_sw7), ._7(dipswitch_2_sw8),
    ._8(dipswitch_2_sw9), ._9(dipswitch_2_sw10), ._10(dipswitch_2_sw11), ._11(dipswitch_2_sw12),
    ._12(dipswitch_2_sw13), ._13(dipswitch_2_sw14), ._14(dipswitch_2_sw15), ._15(dipswitch_2_sw16));
  base_2_decoder base_2_decoder_1 (
    .out_15(base_2_decoder_1_out_15), .e_2(base_2_decoder_1_e_2), .f_2(base_2_decoder_1_f_2),
    .g_2(base_2_decoder_1_g_2), .a(base_2_decoder_1_a), .b(base_2_decoder_1_b), .c(base_2_decoder_1_c),
    .out_8(base_2_decoder_1_out_8), .e(base_2_decoder_1_e), .f(base_2_decoder_1_f), .g(base_2_decoder_1_g),
    .a_2(base_2_decoder_1_a_2), .b_2(base_2_decoder_1_b_2), .c_2(base_2_decoder_1_c_2),
    .B3(calculator_1_out_11), .B2(calculator_1_out_12), .B1(calculator_1_out_13), .B0(calculator_1_out_14));
  _7_Segment_Display u_7_segment_display_5 (
    .g(base_2_decoder_1_g), .f(base_2_decoder_1_f), .a(base_2_decoder_1_a), .b(base_2_decoder_1_b),
    .e(base_2_decoder_1_e), .d(base_2_decoder_1_out_8), .c(base_2_decoder_1_c));  // open: dp
  _7_Segment_Display u_7_segment_display_6 (
    .g(base_2_decoder_1_g_2), .f(base_2_decoder_1_f_2), .a(base_2_decoder_1_a_2), .b(base_2_decoder_1_b_2),
    .e(base_2_decoder_1_e_2), .d(base_2_decoder_1_out_15), .c(base_2_decoder_1_c_2));  // open: dp

  // Notes on the sheet:
  //   Toggle Subtraction
  //   Input 1
  //   Input 2
endmodule

module base_2_encoder (
  input  _0,
  input  _1,
  input  _2,
  input  _3,
  input  _4,
  input  _5,
  input  _6,
  input  _7,
  input  _8,
  input  _9,
  input  _10,
  input  _11,
  input  _12,
  input  _13,
  input  _14,
  input  _15,
  output A0,
  output A1,
  output A2,
  output A3
);

  wire or_1_out, or_2_out, or_3_out, or_4_out, or_5_out, or_6_out, or_7_out, or_8_out, or_9_out, or_10_out,
       or_11_out, or_12_out, or_13_out, or_14_out, or_15_out, or_16_out, or_17_out, or_18_out;

  or or_1 (or_1_out, _13, _15);
  or or_2 (or_2_out, _2, _3);
  or or_3 (or_3_out, _4, _5);
  or or_4 (or_4_out, _6, _7);
  or or_5 (or_5_out, _8, _9);
  or or_6 (or_6_out, _10, _11);
  or or_7 (or_7_out, _12, _13);
  or or_8 (or_8_out, _14, _15);
  or or_9 (or_9_out, _11, or_1_out);
  or or_10 (or_10_out, _9, or_9_out);
  or or_11 (or_11_out, or_2_out, or_4_out);
  or or_12 (or_12_out, or_3_out, or_4_out);
  or or_13 (or_13_out, _5, or_14_out);
  or or_14 (or_14_out, _7, or_10_out);
  or or_15 (or_15_out, or_6_out, or_8_out);
  or or_16 (or_16_out, or_5_out, or_6_out);
  or or_17 (or_17_out, or_7_out, or_8_out);
  or or_18 (or_18_out, _3, or_13_out);
  or or_19 (A0, _1, or_18_out);
  or or_20 (A1, or_11_out, or_15_out);
  or or_21 (A2, or_12_out, or_17_out);
  or or_22 (A3, or_16_out, or_17_out);
endmodule

module half_adder (
  input  A,
  input  in_2,
  output Sum,
  output Carry
);

  xor xor_1 (Sum, in_2, A);
  and and_1 (Carry, in_2, A);

  // Notes on the sheet:
  //   B
endmodule

module full_adder (
  input  A,
  input  B,
  input  in_3,
  output out_4,
  output Sum
);

  wire half_adder_1_carry, half_adder_1_sum, half_adder_2_carry;

  half_adder half_adder_1 (.Sum(half_adder_1_sum), .Carry(half_adder_1_carry), .A(A), .in_2(B));
  half_adder half_adder_2 (.Sum(Sum), .Carry(half_adder_2_carry), .A(half_adder_1_sum), .in_2(in_3));
  or or_1 (out_4, half_adder_1_carry, half_adder_2_carry);

  // Notes on the sheet:
  //   Carry in
  //   Carry out
endmodule

module mux (
  input  in_1,
  input  B,
  input  A,
  output Y
);

  wire and_1_out, and_2_out, not_1_out;

  not not_1 (not_1_out, in_1);
  and and_1 (and_1_out, not_1_out, B);
  and and_2 (and_2_out, in_1, A);
  or or_1 (Y, and_1_out, and_2_out);

  // Notes on the sheet:
  //   Selector
endmodule

module calculator (
  input  A3,
  input  A2,
  input  A1,
  input  A0,
  input  B2,
  input  B1,
  input  B0,
  input  in_8,
  input  Subtract,
  output Overflow,
  output out_11,
  output out_12,
  output out_13,
  output out_14
);

  wire full_adder_2_out_4, full_adder_3_out_4, full_adder_4_out_4, mux_1_y, mux_2_y, mux_3_y, mux_4_y,
       not_1_out, not_2_out, not_3_out, not_4_out;

  full_adder full_adder_1 (.out_4(Overflow), .Sum(out_11), .A(A3), .B(mux_1_y), .in_3(full_adder_2_out_4));
  not not_1 (not_1_out, B2);
  mux mux_1 (.Y(mux_1_y), .B(B2), .A(not_1_out), .in_1(Subtract));
  not not_2 (not_2_out, B1);
  mux mux_2 (.Y(mux_2_y), .B(B1), .A(not_2_out), .in_1(Subtract));
  full_adder full_adder_2 (.out_4(full_adder_2_out_4), .Sum(out_12), .A(A2), .B(mux_2_y), .in_3(full_adder_3_out_4));
  mux mux_3 (.Y(mux_3_y), .B(B0), .A(not_3_out), .in_1(Subtract));
  full_adder full_adder_3 (.out_4(full_adder_3_out_4), .Sum(out_13), .A(A1), .B(mux_3_y), .in_3(full_adder_4_out_4));
  not not_3 (not_3_out, B0);
  full_adder full_adder_4 (.out_4(full_adder_4_out_4), .Sum(out_14), .A(A0), .B(mux_4_y), .in_3(Subtract));
  not not_4 (not_4_out, in_8);
  mux mux_4 (.Y(mux_4_y), .B(in_8), .A(not_4_out), .in_1(Subtract));

  // Notes on the sheet:
  //   B3
  //   S3
  //   S2
  //   S1
  //   S0
endmodule

module operator (
  input  in_1,
  output [4:0] c0,
  output [4:0] c1,
  output [4:0] c2,
  output [4:0] c3,
  output [4:0] out_6
);

  wire [4:0] bit_extender_1_out, not_1_out;

  assign bit_extender_1_out = {{4{in_1}}, in_1};  // Bit_Extender bit_extender_1
  assign not_1_out = ~bit_extender_1_out;  // NOT_Gate not_1, 5 bits wide
  assign c2 = 5'b00100 | not_1_out;  // OR_Gate or_1, 5 bits wide

  assign c0 = 5'b00100;
  assign c1 = 5'b00100;
  assign c3 = 5'b00100;
  assign out_6 = 5'b00100;

  // Notes on the sheet:
  //   Subtract
  //   c4
endmodule

module base_2_decoder (
  input  B3,
  input  B2,
  input  B1,
  input  B0,
  output a,
  output b,
  output c,
  output out_8,
  output e,
  output f,
  output g,
  output a_2,
  output b_2,
  output c_2,
  output out_15,
  output e_2,
  output f_2,
  output g_2
);

  wire and_1_out, and_2_out, and_3_out, and_4_out, and_5_out, and_6_out, and_7_out, and_8_out, and_9_out,
       and_10_out, and_11_out, and_12_out, and_13_out, and_14_out, and_15_out, and_16_out, and_17_out,
       and_18_out, and_19_out, and_20_out, and_21_out, and_22_out, and_23_out, and_24_out, and_25_out,
       and_26_out, and_27_out, nor_1_out, nor_2_out, nor_3_out, nor_4_out, nor_5_out, not_1_out, not_2_out,
       not_3_out, not_4_out, or_2_out, or_3_out, or_4_out, or_5_out, or_6_out, or_7_out, or_9_out, or_10_out,
       or_11_out, or_12_out, or_13_out, or_14_out, or_17_out, or_18_out, or_19_out, or_23_out, or_24_out,
       or_26_out;

  not not_1 (not_1_out, B3);
  not not_2 (not_2_out, B2);
  not not_3 (not_3_out, B1);
  not not_4 (not_4_out, B0);
  and and_1 (and_1_out, B3, B2);
  and and_2 (and_2_out, B3, B1);
  and and_3 (and_3_out, B3, B0);
  and and_4 (and_4_out, B2, B1);
  and and_5 (and_5_out, B2, B0);
  and and_6 (and_6_out, B1, B0);
  nor nor_1 (nor_1_out, B3, B2);
  nor nor_2 (nor_2_out, B3, B1);
  nor nor_3 (nor_3_out, B2, B1);
  nor nor_4 (nor_4_out, B2, B0);
  nor nor_5 (nor_5_out, B1, B0);
  or or_1 (g, and_1_out, and_2_out);
  and and_7 (and_7_out, and_6_out, B2);
  and and_8 (and_8_out, and_1_out, not_3_out);
  and and_9 (and_9_out, nor_5_out, not_1_out);
  and and_10 (and_10_out, not_2_out, B1);
  and and_11 (and_11_out, and_2_out, not_4_out);
  or or_2 (or_2_out, and_5_out, nor_4_out);
  and and_12 (and_12_out, not_1_out, and_6_out);
  or or_3 (or_3_out, and_2_out, nor_2_out);
  and and_13 (and_13_out, B0, not_2_out);
  and and_14 (and_14_out, B3, not_2_out);
  and and_15 (and_15_out, not_4_out, and_4_out);
  or or_4 (or_4_out, not_1_out, B1);
  or or_5 (or_5_out, and_5_out, nor_4_out);
  and and_16 (and_16_out, and_1_out, nor_5_out);
  and and_17 (and_17_out, not_1_out, nor_5_out);
  and and_18 (and_18_out, B2, nor_2_out);
  and and_19 (and_19_out, B1, and_1_out);
  and and_20 (and_20_out, not_4_out, and_2_out);
  and and_21 (and_21_out, and_3_out, nor_3_out);
  and and_22 (and_22_out, not_3_out, B3);
  and and_23 (and_23_out, nor_1_out, B1);
  and and_24 (and_24_out, nor_5_out, B2);
  and and_25 (and_25_out, B2, nor_5_out);
  or or_6 (or_6_out, nor_1_out, g);
  or or_7 (or_7_out, and_7_out, nor_3_out);
  or or_8 (f, nor_1_out, and_9_out);
  or or_9 (or_9_out, and_10_out, and_11_out);
  or or_10 (or_10_out, and_8_out, and_12_out);
  or or_11 (or_11_out, and_3_out, or_3_out);
  or or_12 (or_12_out, and_14_out, and_15_out);
  and and_26 (and_26_out, or_4_out, or_5_out);
  or or_13 (or_13_out, and_20_out, and_21_out);
  or or_14 (or_14_out, and_23_out, and_24_out);
  or or_15 (a, and_25_out, or_6_out);
  or or_16 (c, or_7_out, not_1_out);
  or or_17 (or_17_out, f, or_9_out);
  or or_18 (or_18_out, and_13_out, or_12_out);
  and and_27 (and_27_out, and_15_out, B3);
  or or_19 (or_19_out, and_22_out, or_14_out);
  or or_20 (e, and_8_out, or_17_out);
  or or_21 (a_2, or_2_out, or_10_out);
  or or_22 (e_2, and_26_out, and_16_out);
  or or_23 (or_23_out, and_19_out, or_13_out);
  or or_24 (or_24_out, and_12_out, and_27_out);
  or or_25 (c_2, or_11_out, or_18_out);
  or or_26 (or_26_out, and_18_out, or_23_out);
  or or_27 (g_2, or_24_out, or_19_out);
  or or_28 (f_2, and_17_out, or_26_out);

  assign b = 1'b1;
  assign b_2 = 1'b1;
  assign out_8 = a;
  assign out_15 = a_2;

  // Notes on the sheet:
  //   32
  //   31
  //   21
  //   20
  //   10
  //   32
  //   31
  //   21
  //   20
  //   10
  //   Five's digit
  //   d
  //   Five's digit
  //   d
endmodule
